// Logisim project Display_7_Segment - copia 2.circ as structural Verilog: 5 circuits, main circuit main
module main (
  input  [5:0] in_1
);

  wire action_decoder_1_go, action_decoder_1_left_go, action_decoder_1_right_go, action_decoder_1_stop,
       binary_to_two_seven_segment_1_a, binary_to_two_seven_segment_1_aa, binary_to_two_seven_segment_1_b,
       binary_to_two_seven_segment_1_bb, binary_to_two_seven_segment_1_c, binary_to_two_seven_segment_1_cc,
       binary_to_two_seven_segment_1_d, binary_to_two_seven_segment_1_dd, binary_to_two_seven_segment_1_e,
       binary_to_two_seven_segment_1_ee, binary_to_two_seven_segment_1_f, binary_to_two_seven_segment_1_ff,
       binary_to_two_seven_segment_1_g, binary_to_two_seven_segment_1_gg, binary_to_two_seven_segment_2_a,
       binary_to_two_seven_segment_2_aa, binary_to_two_seven_segment_2_b, binary_to_two_seven_segment_2_bb,
       binary_to_two_seven_segment_2_c, binary_to_two_seven_segment_2_cc, binary_to_two_seven_segment_2_d,
       binary_to_two_seven_segment_2_dd, binary_to_two_seven_segment_2_e, binary_to_two_seven_segment_2_ee,
       binary_to_two_seven_segment_2_f, binary_to_two_seven_segment_2_ff, binary_to_two_seven_segment_2_g,
       binary_to_two_seven_segment_2_gg;
  wire [7:0] movement_control_1_action_decoder_output, movement_control_1_actual_position_output,
       movement_control_1_next_position_output;

  Binary_to_Two_Seven_Segment binary_to_two_seven_segment_1 (
    .dd(binary_to_two_seven_segment_1_dd), .ee(binary_to_two_seven_segment_1_ee),
    .ff(binary_to_two_seven_segment_1_ff), .gg(binary_to_two_seven_segment_1_gg),
    .a(binary_to_two_seven_segment_1_a), .b(binary_to_two_seven_segment_1_b),
    .c(binary_to_two_seven_segment_1_c), .d(binary_to_two_seven_segment_1_d),
    .e(binary_to_two_seven_segment_1_e), .f(binary_to_two_seven_segment_1_f),
    .g(binary_to_two_seven_segment_1_g), .aa(binary_to_two_seven_segment_1_aa),
    .bb(binary_to_two_seven_segment_1_bb), .cc(binary_to_two_seven_segment_1_cc),
    .Entrance(movement_control_1_actual_position_output));
  Movement_Control movement_control_1 (
    .Actual_Position_Output(movement_control_1_actual_position_output),
    .Action_Decoder_Output(movement_control_1_action_decoder_output),
    .Next_Position_Output(movement_control_1_next_position_output), .Entrance(in_1));
  _7_Segment_Display u_7_segment_display_1 (
    .g(binary_to_two_seven_segment_1_g), .f(binary_to_two_seven_segment_1_f),
    .a(binary_to_two_seven_segment_1_a), .b(binary_to_two_seven_segment_1_b),
    .e(binary_to_two_seven_segment_1_e), .d(binary_to_two_seven_segment_1_d),
    .c(binary_to_two_seven_segment_1_c));  // open: dp
  Binary_to_Two_Seven_Segment binary_to_two_seven_segment_2 (
    .dd(binary_to_two_seven_segment_2_dd), .ee(binary_to_two_seven_segment_2_ee),
    .ff(binary_to_two_seven_segment_2_ff), .gg(binary_to_two_seven_segment_2_gg),
    .a(binary_to_two_seven_segment_2_a), .b(binary_to_two_seven_segment_2_b),
    .c(binary_to_two_seven_segment_2_c), .d(binary_to_two_seven_segment_2_d),
    .e(binary_to_two_seven_segment_2_e), .f(binary_to_two_seven_segment_2_f),
    .g(binary_to_two_seven_segment_2_g), .aa(binary_to_two_seven_segment_2_aa),
    .bb(binary_to_two_seven_segment_2_bb), .cc(binary_to_two_seven_segment_2_cc),
    .Entrance(movement_control_1_next_position_output));
  _7_Segment_Display u_7_segment_display_2 (
    .g(binary_to_two_seven_segment_1_gg), .f(binary_to_two_seven_segment_1_ff),
    .a(binary_to_two_seven_segment_1_aa), .b(binary_to_two_seven_segment_1_bb),
    .e(binary_to_two_seven_segment_1_ee), .d(binary_to_two_seven_segment_1_dd),
    .c(binary_to_two_seven_segment_1_cc));  // open: dp
  _7_Segment_Display u_7_segment_display_3 (
    .g(binary_to_two_seven_segment_2_g), .f(binary_to_two_seven_segment_2_f),
    .a(binary_to_two_seven_segment_2_a), .b(binary_to_two_seven_segment_2_b),
    .e(binary_to_two_seven_segment_2_e), .d(binary_to_two_seven_segment_2_d),
    .c(binary_to_two_seven_segment_2_c));  // open: dp
  _7_Segment_Display u_7_segment_display_4 (
    .g(binary_to_two_seven_segment_2_gg), .f(binary_to_two_seven_segment_2_ff),
    .a(binary_to_two_seven_segment_2_aa), .b(binary_to_two_seven_segment_2_bb),
    .e(binary_to_two_seven_segment_2_ee), .d(binary_to_two_seven_segment_2_dd),
    .c(binary_to_two_seven_segment_2_cc));  // open: dp
  LED Go (.in(action_decoder_1_go));
  Action_Decoder action_decoder_1 (
    .Entrance(movement_control_1_action_decoder_output), .Go(action_decoder_1_go),
    .Stop(action_decoder_1_stop), .Right_Go(action_decoder_1_right_go), .Left_Go(action_decoder_1_left_go));
  LED Stop (.in(action_decoder_1_stop));
  LED Right_Go (.in(action_decoder_1_right_go));
  LED Left_Go (.in(action_decoder_1_left_go));
endmodule

module Movement_Control (
  input  [5:0] Entrance,
  output [7:0] Next_Position_Output,
  output [7:0] Action_Decoder_Output,
  output [7:0] Actual_Position_Output
);

  ROM #(.addrWidth(6)) Next_Position (.addr(Entrance), .data(Action_Decoder_Output));
  ROM #(.addrWidth(6)) Actual_Position (.addr(Entrance), .data(Actual_Position_Output));

  assign Next_Position_Output = Action_Decoder_Output;

  // Notes on the sheet:
  //   contents of Next_Position (hex, n*v repeats v):
  //   11 ff ff 42 49 ff 29 9 61 0 ff ff 32 31 ff ff 25 22 60 41 38 12 27 52 37 23 ff 54 4 8 ff 43 33 3 24
  //   ff 16 20 7 ff 6 36 28 40 5*ff 17 ff ff 55 ff 13 34 21 ff ff ff 56 19 ff ff
  //   contents of Actual_Position (hex, n*v repeats v):
  //   0 1 2 3 4 5 6 7 8 9 10 11 12 13 14 15 16 17 18 19 20 21 22 23 24 25 26 27 28 29 30 31 32 33 34 35 36
  //   37 38 39 40 41 42 43 44 45 46 47 48 49 50 51 52 53 54 55 56 57 58 59 60
endmodule

module Sub_Seven_Segment_Decoder (
  input  in_1,
  input  in_2,
  input  in_3,
  input  in_4,
  output a,
  output b,
  output c,
  output d,
  output e,
  output f,
  output g
);

  wire nand_1_out, nand_2_out, nand_3_out, nand_4_out, nand_5_out, nand_6_out, nand_7_out, nand_8_out,
       nand_9_out, nand_10_out, nand_11_out, nand_12_out, nand_13_out, nand_14_out, nand_15_out, nand_16_out,
       nand_17_out, nand_18_out, nand_19_out, nand_20_out, nand_21_out, nand_22_out, nand_23_out,
       nand_24_out, nand_25_out, nand_26_out, nand_27_out, nand_28_out, nand_29_out, nand_30_out,
       nand_31_out, nand_32_out, nand_33_out, nand_34_out, nand_35_out, nand_36_out, nand_37_out,
       nand_38_out, nand_39_out, nand_40_out, nand_41_out, nand_42_out, nand_43_out, nand_44_out,
       nand_45_out, nand_46_out, nand_47_out, nand_48_out, nand_49_out, nand_50_out, nand_51_out,
       nand_52_out, nand_53_out, nand_54_out, nand_55_out, nand_56_out, nand_57_out, nand_58_out,
       nand_59_out, nand_60_out, nand_61_out, nand_62_out, nand_63_out, nand_64_out, nand_65_out,
       nand_66_out, nand_67_out, nand_68_out, nand_69_out, nand_70_out, nand_71_out, nand_72_out,
       nand_73_out, nand_74_out, nand_75_out, nand_76_out, nand_77_out, nand_78_out, nand_79_out,
       nand_80_out, nand_81_out, nand_82_out, nand_83_out, nand_84_out, nand_85_out, nand_86_out,
       nand_87_out, nand_88_out, nand_89_out, nand_90_out, nand_91_out, nand_92_out, nand_93_out,
       nand_94_out, nand_95_out, nand_96_out, nand_97_out, nand_98_out, nand_99_out, nand_100_out,
       nand_101_out, nand_102_out, nand_103_out, nand_104_out, nand_106_out, nand_107_out, nand_108_out,
       nand_109_out, nand_110_out, nand_111_out, nand_112_out, nand_113_out, nand_114_out, nand_115_out,
       nand_116_out, nand_117_out, nand_118_out, nand_119_out, nand_120_out, nand_121_out, nand_122_out,
       nand_123_out, nand_124_out, nand_125_out, nand_126_out, nand_127_out, nand_128_out, nand_129_out,
       nand_130_out, nand_131_out, nand_132_out, nand_133_out, nand_134_out, nand_136_out, nand_137_out,
       nand_138_out, nand_139_out, nand_141_out, nand_142_out, nand_143_out, nand_144_out, nand_145_out,
       nand_146_out, nand_147_out, nand_148_out;

  nand nand_1 (nand_1_out, in_2, in_2);
  nand nand_2 (nand_2_out, in_1, in_1);
  nand nand_3 (nand_3_out, in_3, in_3);
  nand nand_4 (nand_4_out, in_1, in_1);
  nand nand_5 (nand_5_out, in_3, in_3);
  nand nand_6 (nand_6_out, in_1, in_1);
  nand nand_7 (nand_7_out, in_1, in_1);
  nand nand_8 (nand_8_out, in_2, in_2);
  nand nand_9 (nand_9_out, in_2, in_2);
  nand nand_10 (nand_10_out, in_2, in_2);
  nand nand_11 (nand_11_out, in_4, in_4);
  nand nand_12 (nand_12_out, in_4, in_4);
  nand nand_13 (nand_13_out, in_1, in_1);
  nand nand_14 (nand_14_out, in_2, in_2);
  nand nand_15 (nand_15_out, in_4, in_4);
  nand nand_16 (nand_16_out, in_1, in_1);
  nand nand_17 (nand_17_out, in_1, nand_1_out);
  nand nand_18 (nand_18_out, nand_2_out, nand_3_out);
  nand nand_19 (nand_19_out, nand_4_out, nand_5_out);
  nand nand_20 (nand_20_out, nand_6_out, in_4);
  nand nand_21 (nand_21_out, nand_7_out, nand_8_out);
  nand nand_22 (nand_22_out, nand_9_out, in_3);
  nand nand_23 (nand_23_out, nand_10_out, nand_11_out);
  nand nand_24 (nand_24_out, in_3, nand_12_out);
  nand nand_25 (nand_25_out, in_1, in_3);
  nand nand_26 (nand_26_out, in_1, in_2);
  nand nand_27 (nand_27_out, nand_13_out, in_2);
  nand nand_28 (nand_28_out, nand_14_out, in_3);
  nand nand_29 (nand_29_out, in_3, nand_15_out);
  nand nand_30 (nand_30_out, nand_16_out, in_2);
  nand nand_31 (nand_31_out, in_2, in_2);
  nand nand_32 (nand_32_out, in_4, in_4);
  nand nand_33 (nand_33_out, in_1, in_1);
  nand nand_34 (nand_34_out, in_1, in_1);
  nand nand_35 (nand_35_out, nand_17_out, nand_17_out);
  nand nand_36 (nand_36_out, in_3, in_3);
  nand nand_37 (nand_37_out, in_1, in_1);
  nand nand_38 (nand_38_out, in_2, in_2);
  nand nand_39 (nand_39_out, nand_18_out, nand_18_out);
  nand nand_40 (nand_40_out, in_4, in_4);
  nand nand_41 (nand_41_out, in_1, in_1);
  nand nand_42 (nand_42_out, in_3, in_3);
  nand nand_43 (nand_43_out, nand_19_out, nand_20_out);
  nand nand_44 (nand_44_out, in_3, in_3);
  nand nand_45 (nand_45_out, in_1, in_1);
  nand nand_46 (nand_46_out, in_2, in_2);
  nand nand_47 (nand_47_out, nand_21_out, nand_21_out);
  nand nand_48 (nand_48_out, in_4, in_4);
  nand nand_49 (nand_49_out, nand_22_out, nand_22_out);
  nand nand_50 (nand_50_out, in_3, in_3);
  nand nand_51 (nand_51_out, in_3, in_3);
  nand nand_52 (nand_52_out, nand_23_out, nand_24_out);
  nand nand_53 (nand_53_out, nand_25_out, nand_26_out);
  nand nand_54 (nand_54_out, in_3, in_3);
  nand nand_55 (nand_55_out, in_4, in_4);
  nand nand_56 (nand_56_out, nand_27_out, nand_27_out);
  nand nand_57 (nand_57_out, in_3, in_3);
  nand nand_58 (nand_58_out, nand_28_out, nand_29_out);
  nand nand_59 (nand_59_out, nand_30_out, nand_30_out);
  nand nand_60 (nand_60_out, in_3, in_3);
  nand nand_61 (nand_61_out, in_2, in_2);
  nand nand_62 (nand_62_out, nand_31_out, nand_32_out);
  nand nand_63 (nand_63_out, nand_33_out, in_3);
  nand nand_64 (nand_64_out, nand_34_out, in_2);
  nand nand_65 (nand_65_out, in_2, in_3);
  nand nand_66 (nand_66_out, nand_35_out, nand_36_out);
  nand nand_67 (nand_67_out, nand_37_out, nand_38_out);
  nand nand_68 (nand_68_out, nand_39_out, nand_40_out);
  nand nand_69 (nand_69_out, nand_41_out, in_3);
  nand nand_70 (nand_70_out, in_1, nand_42_out);
  nand nand_71 (nand_71_out, nand_43_out, nand_43_out);
  nand nand_72 (nand_72_out, nand_44_out, in_4);
  nand nand_73 (nand_73_out, nand_45_out, in_2);
  nand nand_74 (nand_74_out, in_1, nand_46_out);
  nand nand_75 (nand_75_out, nand_47_out, nand_48_out);
  nand nand_76 (nand_76_out, nand_49_out, in_4);
  nand nand_77 (nand_77_out, in_2, nand_50_out);
  nand nand_78 (nand_78_out, in_2, in_3);
  nand nand_79 (nand_79_out, in_1, nand_51_out);
  nand nand_80 (nand_80_out, nand_52_out, nand_52_out);
  nand nand_81 (nand_81_out, nand_53_out, nand_53_out);
  nand nand_82 (nand_82_out, nand_54_out, nand_55_out);
  nand nand_83 (nand_83_out, nand_56_out, nand_57_out);
  nand nand_84 (nand_84_out, nand_58_out, nand_58_out);
  nand nand_85 (nand_85_out, nand_59_out, nand_60_out);
  nand nand_86 (nand_86_out, in_1, nand_61_out);
  nand nand_87 (nand_87_out, in_1, in_4);
  nand nand_88 (nand_88_out, nand_62_out, nand_63_out);
  nand nand_89 (nand_89_out, nand_64_out, nand_64_out);
  nand nand_90 (nand_90_out, nand_65_out, nand_66_out);
  nand nand_91 (nand_91_out, in_4, in_4);
  nand nand_92 (nand_92_out, nand_67_out, nand_68_out);
  nand nand_93 (nand_93_out, in_2, in_2);
  nand nand_94 (nand_94_out, in_4, in_4);
  nand nand_95 (nand_95_out, nand_69_out, nand_69_out);
  nand nand_96 (nand_96_out, nand_70_out, nand_70_out);
  nand nand_97 (nand_97_out, nand_71_out, nand_72_out);
  nand nand_98 (nand_98_out, nand_73_out, nand_74_out);
  nand nand_99 (nand_99_out, nand_75_out, nand_76_out);
  nand nand_100 (nand_100_out, nand_77_out, nand_77_out);
  nand nand_101 (nand_101_out, nand_78_out, nand_78_out);
  nand nand_102 (nand_102_out, in_4, in_4);
  nand nand_103 (nand_103_out, nand_79_out, nand_79_out);
  nand nand_104 (nand_104_out, in_4, in_4);
  nand nand_105 (e, nand_80_out, nand_81_out);
  nand nand_106 (nand_106_out, nand_82_out, nand_83_out);
  nand nand_107 (nand_107_out, in_4, in_4);
  nand nand_108 (nand_108_out, in_2, in_2);
  nand nand_109 (nand_109_out, nand_84_out, nand_85_out);
  nand nand_110 (nand_110_out, nand_86_out, nand_87_out);
  nand nand_111 (nand_111_out, nand_88_out, nand_88_out);
  nand nand_112 (nand_112_out, nand_89_out, in_4);
  nand nand_113 (nand_113_out, nand_90_out, nand_90_out);
  nand nand_114 (nand_114_out, in_1, nand_91_out);
  nand nand_115 (nand_115_out, nand_92_out, nand_92_out);
  nand nand_116 (nand_116_out, nand_93_out, nand_94_out);
  nand nand_117 (nand_117_out, nand_95_out, in_4);
  nand nand_118 (nand_118_out, nand_96_out, in_4);
  nand nand_119 (nand_119_out, nand_97_out, nand_97_out);
  nand nand_120 (nand_120_out, nand_98_out, nand_98_out);
  nand nand_121 (nand_121_out, nand_99_out, nand_99_out);
  nand nand_122 (nand_122_out, nand_100_out, in_4);
  nand nand_123 (nand_123_out, nand_101_out, nand_102_out);
  nand nand_124 (nand_124_out, nand_103_out, nand_104_out);
  nand nand_125 (nand_125_out, nand_106_out, nand_106_out);
  nand nand_126 (nand_126_out, in_2, nand_107_out);
  nand nand_127 (nand_127_out, in_1, nand_108_out);
  nand nand_128 (nand_128_out, in_1, in_3);
  nand nand_129 (nand_129_out, nand_109_out, nand_109_out);
  nand nand_130 (nand_130_out, nand_110_out, nand_110_out);
  nand nand_131 (nand_131_out, nand_111_out, nand_112_out);
  nand nand_132 (nand_132_out, nand_113_out, nand_114_out);
  nand nand_133 (nand_133_out, nand_115_out, nand_116_out);
  nand nand_134 (nand_134_out, nand_117_out, nand_118_out);
  nand nand_135 (c, nand_119_out, nand_120_out);
  nand nand_136 (nand_136_out, nand_121_out, nand_122_out);
  nand nand_137 (nand_137_out, nand_123_out, nand_124_out);
  nand nand_138 (nand_138_out, nand_125_out, nand_126_out);
  nand nand_139 (nand_139_out, nand_127_out, nand_128_out);
  nand nand_140 (g, nand_129_out, nand_130_out);
  nand nand_141 (nand_141_out, nand_131_out, nand_131_out);
  nand nand_142 (nand_142_out, nand_132_out, nand_132_out);
  nand nand_143 (nand_143_out, nand_133_out, nand_133_out);
  nand nand_144 (nand_144_out, nand_134_out, nand_134_out);
  nand nand_145 (nand_145_out, nand_136_out, nand_136_out);
  nand nand_146 (nand_146_out, nand_137_out, nand_137_out);
  nand nand_147 (nand_147_out, nand_138_out, nand_138_out);
  nand nand_148 (nand_148_out, nand_139_out, nand_139_out);
  nand nand_149 (a, nand_141_out, nand_142_out);
  nand nand_150 (b, nand_143_out, nand_144_out);
  nand nand_151 (d, nand_145_out, nand_146_out);
  nand nand_152 (f, nand_147_out, nand_148_out);
endmodule

module Binary_to_Two_Seven_Segment (
  input  [7:0] Entrance,
  output aa,
  output bb,
  output cc,
  output dd,
  output ee,
  output ff,
  output gg,
  output a,
  output b,
  output c,
  output d,
  output e,
  output f,
  output g
);

  Sub_Seven_Segment_Decoder sub_seven_segment_decoder_1 (
    .c(cc), .d(dd), .e(ee), .f(ff), .a(aa), .g(gg), .b(bb), .in_3(Entrance[1]), .in_4(Entrance[0]),
    .in_1(Entrance[3]), .in_2(Entrance[2]));
  Sub_Seven_Segment_Decoder sub_seven_segment_decoder_2 (
    .c(c), .d(d), .e(e), .f(f), .a(a), .g(g), .b(b), .in_3(Entrance[5]), .in_4(Entrance[4]),
    .in_1(Entrance[7]), .in_2(Entrance[6]));

  // Notes on the sheet:
  //   Second_Number
  //   First_Number
endmodule

module Action_Decoder (
  input  [7:0] Entrance,
  output Go,
  output Stop,
  output Right_Go,
  output Left_Go
);

  wire not_1_out, not_2_out, not_3_out, not_4_out;
  wire [7:0] rom_1_data;

  ROM rom_1 (.addr(Entrance), .data(rom_1_data));
  not not_1 (not_1_out, rom_1_data[4]);
  not not_2 (not_2_out, rom_1_data[4]);
  not not_3 (not_3_out, rom_1_data[0]);
  not not_4 (not_4_out, rom_1_data[0]);
  and and_1 (Go, rom_1_data[0], not_1_out);
  and and_2 (Stop, rom_1_data[4], rom_1_data[0]);
  and and_3 (Right_Go, not_2_out, not_3_out);
  and and_4 (Left_Go, rom_1_data[4], not_4_out);

  // Notes on the sheet:
  //   contents of rom_1 (hex, n*v repeats v):
  //   10 ff ff 1 10 ff 0 0 1 10 7*ff 1 1 1 ff ff 1 1 ff 1 6*ff 1 0 0 10 1 10 ff 1 0 10 7*ff 10 0 1 10 ff 0
  //   0 0 7*ff 0 0 0 10 5*ff 1 8*ff 1 ff 10 1 10 9*ff 1 10 157*ff 11
endmodule
