// Logisim project Display_7_Segment.circ as structural Verilog
module Movement_Control (
  input  [3:0] in_1,
  input  [5:0] in_2,
  input  [5:0] in_3
);

  wire l_7_segment_display_driver_f95ed3f6_1_p1, l_7_segment_display_driver_f95ed3f6_1_p2,
       l_7_segment_display_driver_f95ed3f6_1_p5, l_7_segment_display_driver_f95ed3f6_1_p6,
       l_7_segment_display_driver_f95ed3f6_1_p7, l_7_segment_display_driver_f95ed3f6_1_p8,
       l_7_segment_display_driver_f95ed3f6_1_p9, l_7_segment_display_driver_f95ed3f6_1_p10,
       l_7_segment_display_driver_f95ed3f6_1_p11, l_7_segment_display_driver_f95ed3f6_2_p5,
       l_7_segment_display_driver_f95ed3f6_2_p6, l_7_segment_display_driver_f95ed3f6_2_p7,
       l_7_segment_display_driver_f95ed3f6_2_p8, l_7_segment_display_driver_f95ed3f6_2_p9,
       l_7_segment_display_driver_f95ed3f6_2_p10, l_7_segment_display_driver_f95ed3f6_2_p11,
       l_7_segment_display_driver_f95ed3f6_3_p5, l_7_segment_display_driver_f95ed3f6_3_p6,
       l_7_segment_display_driver_f95ed3f6_3_p7, l_7_segment_display_driver_f95ed3f6_3_p8,
       l_7_segment_display_driver_f95ed3f6_3_p9, l_7_segment_display_driver_f95ed3f6_3_p10,
       l_7_segment_display_driver_f95ed3f6_3_p11, l_7_segment_display_driver_f95ed3f6_4_p5,
       l_7_segment_display_driver_f95ed3f6_4_p6, l_7_segment_display_driver_f95ed3f6_4_p7,
       l_7_segment_display_driver_f95ed3f6_4_p8, l_7_segment_display_driver_f95ed3f6_4_p9,
       l_7_segment_display_driver_f95ed3f6_4_p10, l_7_segment_display_driver_f95ed3f6_4_p11,
       l_7_segment_display_driver_f95ed3f6_5_p5, l_7_segment_display_driver_f95ed3f6_5_p6,
       l_7_segment_display_driver_f95ed3f6_5_p7, l_7_segment_display_driver_f95ed3f6_5_p8,
       l_7_segment_display_driver_f95ed3f6_5_p9, l_7_segment_display_driver_f95ed3f6_5_p10,
       l_7_segment_display_driver_f95ed3f6_5_p11;
  wire [3:0] rom_2_data;
  wire [7:0] rom_1_data;

  ROM #(.addrWidth(6)) rom_1 (.addr(in_2), .data(rom_1_data));
  ROM #(.addrWidth(4), .dataWidth(4)) rom_2 (.addr(in_1), .data(rom_2_data));
  // L_7_segment_display_driver_f95ed3f6 l_7_segment_display_driver_f95ed3f6_1: pin names not known; wires that end beside it: l_7_segment_display_driver_f95ed3f6_1_p1, l_7_segment_display_driver_f95ed3f6_1_p2, in_3[5], in_3[4], l_7_segment_display_driver_f95ed3f6_1_p5, l_7_segment_display_driver_f95ed3f6_1_p6, l_7_segment_display_driver_f95ed3f6_1_p7, l_7_segment_display_driver_f95ed3f6_1_p8, l_7_segment_display_driver_f95ed3f6_1_p9, l_7_segment_display_driver_f95ed3f6_1_p10, l_7_segment_display_driver_f95ed3f6_1_p11
  _7_Segment_Display u_7_segment_display_1 (
    .g(l_7_segment_display_driver_f95ed3f6_1_p11), .f(l_7_segment_display_driver_f95ed3f6_1_p10),
    .a(l_7_segment_display_driver_f95ed3f6_1_p5), .b(l_7_segment_display_driver_f95ed3f6_1_p6),
    .e(l_7_segment_display_driver_f95ed3f6_1_p9), .d(l_7_segment_display_driver_f95ed3f6_1_p8),
    .c(l_7_segment_display_driver_f95ed3f6_1_p7));  // open: dp
  // L_7_segment_display_driver_f95ed3f6 l_7_segment_display_driver_f95ed3f6_2: pin names not known; wires that end beside it: in_3[3], in_3[2], in_3[1], in_3[0], l_7_segment_display_driver_f95ed3f6_2_p5, l_7_segment_display_driver_f95ed3f6_2_p6, l_7_segment_display_driver_f95ed3f6_2_p7, l_7_segment_display_driver_f95ed3f6_2_p8, l_7_segment_display_driver_f95ed3f6_2_p9, l_7_segment_display_driver_f95ed3f6_2_p10, l_7_segment_display_driver_f95ed3f6_2_p11
  // L_7_segment_display_driver_f95ed3f6 l_7_segment_display_driver_f95ed3f6_3: pin names not known; wires that end beside it: rom_2_data[3], rom_2_data[2], rom_2_data[1], rom_2_data[0], l_7_segment_display_driver_f95ed3f6_3_p5, l_7_segment_display_driver_f95ed3f6_3_p6, l_7_segment_display_driver_f95ed3f6_3_p7, l_7_segment_display_driver_f95ed3f6_3_p8, l_7_segment_display_driver_f95ed3f6_3_p9, l_7_segment_display_driver_f95ed3f6_3_p10, l_7_segment_display_driver_f95ed3f6_3_p11
  // L_7_segment_display_driver_f95ed3f6 l_7_segment_display_driver_f95ed3f6_4: pin names not known; wires that end beside it: rom_1_data[7], rom_1_data[6], rom_1_data[5], rom_1_data[4], l_7_segment_display_driver_f95ed3f6_4_p5, l_7_segment_display_driver_f95ed3f6_4_p6, l_7_segment_display_driver_f95ed3f6_4_p7, l_7_segment_display_driver_f95ed3f6_4_p8, l_7_segment_display_driver_f95ed3f6_4_p9, l_7_segment_display_driver_f95ed3f6_4_p10, l_7_segment_display_driver_f95ed3f6_4_p11
  _7_Segment_Display u_7_segment_display_2 (
    .g(l_7_segment_display_driver_f95ed3f6_2_p11), .f(l_7_segment_display_driver_f95ed3f6_2_p10),
    .a(l_7_segment_display_driver_f95ed3f6_2_p5), .b(l_7_segment_display_driver_f95ed3f6_2_p6),
    .e(l_7_segment_display_driver_f95ed3f6_2_p9), .d(l_7_segment_display_driver_f95ed3f6_2_p8),
    .c(l_7_segment_display_driver_f95ed3f6_2_p7));  // open: dp
  _7_Segment_Display u_7_segment_display_3 (
    .g(l_7_segment_display_driver_f95ed3f6_3_p11), .f(l_7_segment_display_driver_f95ed3f6_3_p10),
    .a(l_7_segment_display_driver_f95ed3f6_3_p5), .b(l_7_segment_display_driver_f95ed3f6_3_p6),
    .e(l_7_segment_display_driver_f95ed3f6_3_p9), .d(l_7_segment_display_driver_f95ed3f6_3_p8),
    .c(l_7_segment_display_driver_f95ed3f6_3_p7));  // open: dp
  _7_Segment_Display u_7_segment_display_4 (
    .g(l_7_segment_display_driver_f95ed3f6_4_p11), .f(l_7_segment_display_driver_f95ed3f6_4_p10),
    .a(l_7_segment_display_driver_f95ed3f6_4_p5), .b(l_7_segment_display_driver_f95ed3f6_4_p6),
    .e(l_7_segment_display_driver_f95ed3f6_4_p9), .d(l_7_segment_display_driver_f95ed3f6_4_p8),
    .c(l_7_segment_display_driver_f95ed3f6_4_p7));  // open: dp
  // L_7_segment_display_driver_f95ed3f6 l_7_segment_display_driver_f95ed3f6_5: pin names not known; wires that end beside it: rom_1_data[3], rom_1_data[2], rom_1_data[1], rom_1_data[0], l_7_segment_display_driver_f95ed3f6_5_p5, l_7_segment_display_driver_f95ed3f6_5_p6, l_7_segment_display_driver_f95ed3f6_5_p7, l_7_segment_display_driver_f95ed3f6_5_p8, l_7_segment_display_driver_f95ed3f6_5_p9, l_7_segment_display_driver_f95ed3f6_5_p10, l_7_segment_display_driver_f95ed3f6_5_p11
  _7_Segment_Display u_7_segment_display_5 (
    .g(l_7_segment_display_driver_f95ed3f6_5_p11), .f(l_7_segment_display_driver_f95ed3f6_5_p10),
    .a(l_7_segment_display_driver_f95ed3f6_5_p5), .b(l_7_segment_display_driver_f95ed3f6_5_p6),
    .e(l_7_segment_display_driver_f95ed3f6_5_p9), .d(l_7_segment_display_driver_f95ed3f6_5_p8),
    .c(l_7_segment_display_driver_f95ed3f6_5_p7));  // open: dp

  // Notes on the sheet:
  //   contents of rom_1 (hex, n*v repeats v):
  //   18*0 18 41*0 60
  //   contents of rom_2 (hex, n*v repeats v):
  //   2 8
  //   Posición Actual
  //   Siguiente Posición
endmodule
