// Logisim project Movement_Control.circ as structural Verilog: 1 circuit, main circuit main
module main (
  input  a,
  input  b,
  input  c,
  input  d,
  input  e,
  input  f,
  output x,
  output y,
  output z,
  output u,
  output v,
  output w
);

  wire and_1_out, and_2_out, and_3_out, and_4_out, and_5_out, and_6_out, and_7_out, and_8_out, and_9_out,
       and_10_out, and_11_out, and_12_out, and_13_out, and_14_out, and_15_out, and_16_out, and_17_out,
       and_18_out, and_19_out, and_20_out, and_21_out, and_22_out, and_23_out, and_24_out, and_25_out,
       and_26_out, and_27_out, and_28_out, and_29_out, and_30_out, and_31_out, and_32_out, and_33_out,
       and_34_out, and_35_out, and_36_out, and_37_out, and_38_out, and_39_out, and_40_out, and_41_out,
       and_42_out, and_43_out, and_44_out, and_45_out, and_46_out, and_47_out, and_48_out, and_49_out,
       and_50_out, and_51_out, and_52_out, and_53_out, not_1_out, not_2_out, not_3_out, not_4_out, not_5_out,
       not_6_out;

  not not_1 (not_1_out, a);
  not not_2 (not_2_out, b);
  not not_3 (not_3_out, c);
  not not_4 (not_4_out, d);
  not not_5 (not_5_out, e);
  not not_6 (not_6_out, f);
  and and_1 (and_1_out, not_1_out, not_4_out, e);
  and and_2 (and_2_out, not_1_out, not_2_out, d, not_5_out, not_6_out);
  and and_3 (and_3_out, not_1_out, c, not_4_out, not_6_out);
  and and_4 (and_4_out, b, e, f);
  and and_5 (and_5_out, a, not_3_out, not_4_out, not_5_out, not_6_out);
  and and_6 (and_6_out, a, not_2_out, c, f);
  and and_7 (and_7_out, a, b, d, not_5_out, not_6_out);
  and and_8 (and_8_out, not_2_out, e, not_6_out);
  and and_9 (and_9_out, not_2_out, not_3_out, d, not_6_out);
  and and_10 (and_10_out, not_1_out, not_2_out, c, not_4_out, not_6_out);
  and and_11 (and_11_out, not_1_out, c, not_4_out, e);
  and and_12 (and_12_out, not_2_out, c, d, f);
  and and_13 (and_13_out, not_1_out, b, not_3_out, not_6_out);
  and and_14 (and_14_out, b, not_4_out, not_5_out, f);
  and and_15 (and_15_out, not_1_out, b, not_3_out, d, e);
  and and_16 (and_16_out, a, b, not_5_out);
  and and_17 (and_17_out, not_1_out, not_2_out, not_4_out, not_6_out);
  and and_18 (and_18_out, not_1_out, not_3_out, not_4_out, not_6_out);
  and and_19 (and_19_out, not_2_out, e);
  and and_20 (and_20_out, not_3_out, not_4_out, e);
  and and_21 (and_21_out, e, not_6_out);
  and and_22 (and_22_out, not_1_out, d, not_5_out, f);
  and and_23 (and_23_out, c, d, e);
  and and_24 (and_24_out, a, c, d, not_6_out);
  and and_25 (and_25_out, not_1_out, not_2_out, e, not_6_out);
  and and_26 (and_26_out, not_1_out, not_4_out, e, not_6_out);
  and and_27 (and_27_out, not_2_out, d, not_5_out, f);
  and and_28 (and_28_out, c, not_4_out, not_6_out);
  and and_29 (and_29_out, not_1_out, b, not_4_out, not_5_out, f);
  and and_30 (and_30_out, not_1_out, b, not_3_out, d, f);
  and and_31 (and_31_out, not_1_out, b, c, not_6_out);
  and and_32 (and_32_out, b, c, not_4_out);
  and and_33 (and_33_out, a, not_2_out, c, not_5_out);
  and and_34 (and_34_out, a, b, not_3_out, not_6_out);
  and and_35 (and_35_out, not_1_out, not_2_out, not_3_out, not_4_out);
  and and_36 (and_36_out, not_2_out, not_3_out, not_4_out, f);
  and and_37 (and_37_out, not_2_out, d, not_5_out, f);
  and and_38 (and_38_out, not_1_out, c, e);
  and and_39 (and_39_out, not_1_out, b, not_4_out, not_5_out, f);
  and and_40 (and_40_out, not_1_out, b, not_3_out, d, not_6_out);
  and and_41 (and_41_out, a, d, f);
  and and_42 (and_42_out, a, not_2_out, c, not_5_out, not_6_out);
  and and_43 (and_43_out, a, b, not_3_out, not_5_out, not_6_out);
  and and_44 (and_44_out, not_1_out, not_2_out, not_3_out, not_5_out);
  and and_45 (and_45_out, not_1_out, not_4_out, not_5_out, not_6_out);
  and and_46 (and_46_out, not_2_out, d, f);
  and and_47 (and_47_out, d, e, not_6_out);
  and and_48 (and_48_out, c, d, e);
  and and_49 (and_49_out, b, not_3_out, not_5_out, not_6_out);
  and and_50 (and_50_out, b, not_3_out, not_4_out, e, f);
  and and_51 (and_51_out, b, c, not_4_out, not_5_out);
  and and_52 (and_52_out, a, not_3_out, not_4_out, not_5_out);
  and and_53 (and_53_out, a, b, not_5_out, f);
  or or_1 (x, and_1_out, and_2_out, and_3_out, and_4_out, and_5_out, and_6_out, and_7_out);
  or or_2 (y, and_8_out, and_9_out, and_10_out, and_11_out, and_12_out, and_13_out, and_14_out, and_15_out, and_16_out);
  or or_3 (z, and_17_out, and_18_out, and_19_out, and_20_out, and_21_out, and_22_out, and_23_out, and_24_out);
  or or_4 (u, and_25_out, and_26_out, and_27_out, and_28_out, and_29_out, and_30_out, and_31_out, and_32_out, and_33_out, and_34_out);
  or or_5 (v, and_35_out, and_36_out, and_37_out, and_38_out, and_39_out, and_40_out, and_41_out, and_42_out, and_43_out);
  or or_6 (w, and_44_out, and_45_out, and_46_out, and_47_out, and_48_out, and_49_out, and_50_out, and_51_out, and_52_out, and_53_out);
endmodule
