// Logisim project Robot.circ as structural Verilog: 8 circuits, main circuit Main
module Main (
  input  [5:0] in_1
);

  wire action_decoder_1_go, action_decoder_1_left_go, action_decoder_1_right_go, action_decoder_1_stop;
  wire [1:0] movement_control_decoder_1_action;
  wire [5:0] movement_control_decoder_1_next_position;
  wire [6:0] binary_to_two_7_segment_decoder_1_display_1, binary_to_two_7_segment_decoder_1_display_2,
       binary_to_two_7_segment_decoder_2_display_1, binary_to_two_7_segment_decoder_2_display_2;

  Movement_Control_Decoder movement_control_decoder_1 (
    .Next_Position(movement_control_decoder_1_next_position), .Action(movement_control_decoder_1_action),
    .Entrance(in_1));
  Display_Decoder display_decoder_1 (.in_1(binary_to_two_7_segment_decoder_1_display_1));
  Binary_to_Two_7_Segment_Decoder binary_to_two_7_segment_decoder_1 (
    .Display_2(binary_to_two_7_segment_decoder_1_display_2),
    .Display_1(binary_to_two_7_segment_decoder_1_display_1), .Entrance(in_1));
  Display_Decoder display_decoder_2 (.in_1(binary_to_two_7_segment_decoder_1_display_2));
  Action_Decoder action_decoder_1 (
    .Left_Go(action_decoder_1_left_go), .Go(action_decoder_1_go), .Stop(action_decoder_1_stop),
    .Right_Go(action_decoder_1_right_go), .Entrance(movement_control_decoder_1_action));
  Binary_to_Two_7_Segment_Decoder binary_to_two_7_segment_decoder_2 (
    .Display_2(binary_to_two_7_segment_decoder_2_display_2),
    .Display_1(binary_to_two_7_segment_decoder_2_display_1),
    .Entrance(movement_control_decoder_1_next_position));
  LED Right_Go (.in(action_decoder_1_right_go));
  Display_Decoder display_decoder_3 (.in_1(binary_to_two_7_segment_decoder_2_display_1));
  Display_Decoder display_decoder_4 (.in_1(binary_to_two_7_segment_decoder_2_display_2));
  LED Left_Go (.in(action_decoder_1_left_go));
  LED Go (.in(action_decoder_1_go));
  LED Stop (.in(action_decoder_1_stop));

  // Notes on the sheet:
  //   Actual Position
  //   Next Position
endmodule

module Circuit_Movement (
  input  a,
  input  b,
  input  c,
  input  d,
  input  e,
  input  f,
  output u,
  output v,
  output w,
  output x,
  output y,
  output z
);

  wire and_1_out, and_2_out, and_3_out, and_4_out, and_5_out, and_6_out, and_7_out, and_8_out, and_9_out,
       and_10_out, and_11_out, and_12_out, and_13_out, and_14_out, and_15_out, and_16_out, and_17_out,
       and_18_out, and_19_out, and_20_out, and_21_out, and_22_out, and_23_out, and_24_out, and_25_out,
       and_26_out, and_27_out, and_28_out, and_29_out, and_30_out, and_31_out, and_32_out, and_33_out,
       and_34_out, and_35_out, and_36_out, and_37_out, and_38_out, and_39_out, and_40_out, and_41_out,
       and_42_out, and_43_out, and_44_out, and_45_out, and_46_out, and_47_out, and_48_out, and_49_out,
       and_50_out, and_51_out, and_52_out, and_53_out, and_54_out, and_55_out, and_56_out, and_57_out,
       and_58_out, and_59_out, and_60_out, and_61_out, and_62_out, and_63_out, and_64_out, and_65_out,
       and_66_out, and_67_out, and_68_out, and_69_out, and_70_out, and_71_out, and_72_out, and_73_out,
       and_74_out, and_75_out, and_76_out, and_77_out, and_78_out, and_79_out, not_1_out, not_2_out,
       not_3_out, not_4_out, not_5_out, not_6_out;

  not not_1 (not_1_out, a);
  not not_2 (not_2_out, b);
  not not_3 (not_3_out, c);
  not not_4 (not_4_out, d);
  not not_5 (not_5_out, e);
  not not_6 (not_6_out, f);
  and and_1 (and_1_out, not_3_out, not_4_out, e, f);
  and and_2 (and_2_out, not_1_out, not_2_out, d, not_5_out, not_6_out);
  and and_3 (and_3_out, not_1_out, c, not_4_out, not_5_out, not_6_out);
  and and_4 (and_4_out, b, not_3_out, not_4_out, e);
  and and_5 (and_5_out, b, e, f);
  and and_6 (and_6_out, b, not_3_out, d, not_5_out, not_6_out);
  and and_7 (and_7_out, a, not_3_out, not_4_out, not_5_out, not_6_out);
  and and_8 (and_8_out, a, e, f);
  and and_9 (and_9_out, a, c, not_4_out, f);
  and and_10 (and_10_out, a, not_2_out, c, d);
  and and_11 (and_11_out, a, c, d, not_6_out);
  and and_12 (and_12_out, a, b, not_4_out, e);
  and and_13 (and_13_out, a, b, not_3_out, d, not_5_out);
  and and_14 (and_14_out, not_1_out, not_2_out, not_3_out, d, not_6_out);
  and and_15 (and_15_out, not_1_out, not_2_out, c, not_4_out, not_5_out, not_6_out);
  and and_16 (and_16_out, not_1_out, not_2_out, c, d, not_5_out, f);
  and and_17 (and_17_out, b, not_3_out, not_4_out, not_5_out);
  and and_18 (and_18_out, not_1_out, b, e, not_6_out);
  and and_19 (and_19_out, not_1_out, b, not_3_out, d, e);
  and and_20 (and_20_out, b, c, not_4_out, f);
  and and_21 (and_21_out, a, not_4_out, e, not_6_out);
  and and_22 (and_22_out, a, not_3_out, d, not_5_out);
  and and_23 (and_23_out, a, b, not_4_out);
  and and_24 (and_24_out, a, b, c);
  and and_25 (and_25_out, not_1_out, not_2_out, not_4_out, not_5_out, not_6_out);
  and and_26 (and_26_out, not_1_out, not_3_out, not_4_out, e, f);
  and and_27 (and_27_out, not_1_out, not_2_out, d, e);
  and and_28 (and_28_out, not_2_out, c, e);
  and and_29 (and_29_out, c, e, not_6_out);
  and and_30 (and_30_out, not_2_out, c, d, f);
  and and_31 (and_31_out, c, d, e);
  and and_32 (and_32_out, not_1_out, b, not_3_out, not_4_out, not_6_out);
  and and_33 (and_33_out, not_1_out, b, d, not_5_out, f);
  and and_34 (and_34_out, b, d, e, not_6_out);
  and and_35 (and_35_out, a, not_2_out, not_4_out, e, not_6_out);
  and and_36 (and_36_out, a, c, d, not_6_out);
  and and_37 (and_37_out, a, b, c, not_4_out, f);
  and and_38 (and_38_out, not_2_out, d, not_5_out, f);
  and and_39 (and_39_out, not_2_out, d, e, not_6_out);
  and and_40 (and_40_out, c, not_4_out, not_5_out, not_6_out);
  and and_41 (and_41_out, not_2_out, c, d, e);
  and and_42 (and_42_out, not_1_out, b, not_3_out, not_5_out, f);
  and and_43 (and_43_out, not_1_out, b, not_3_out, not_4_out, e, not_6_out);
  and and_44 (and_44_out, b, not_3_out, d, not_5_out);
  and and_45 (and_45_out, not_1_out, b, not_3_out, d, f);
  and and_46 (and_46_out, not_1_out, b, c, not_4_out, f);
  and and_47 (and_47_out, not_1_out, b, c, d, not_6_out);
  and and_48 (and_48_out, a, not_2_out, d, e);
  and and_49 (and_49_out, a, d, e, not_6_out);
  and and_50 (and_50_out, a, not_2_out, c, not_5_out);
  and and_51 (and_51_out, a, not_2_out, c, not_6_out);
  and and_52 (and_52_out, a, c, d, e);
  and and_53 (and_53_out, not_1_out, not_2_out, not_3_out, not_4_out, not_6_out);
  and and_54 (and_54_out, not_1_out, not_2_out, not_4_out, e);
  and and_55 (and_55_out, not_1_out, c, e);
  and and_56 (and_56_out, not_1_out, not_2_out, c, d, f);
  and and_57 (and_57_out, not_1_out, b, not_4_out, not_5_out, f);
  and and_58 (and_58_out, not_1_out, b, not_3_out, d, not_6_out);
  and and_59 (and_59_out, b, not_3_out, d, not_5_out, not_6_out);
  and and_60 (and_60_out, b, c, e);
  and and_61 (and_61_out, a, not_2_out, not_3_out, not_4_out, f);
  and and_62 (and_62_out, a, not_3_out, e, f);
  and and_63 (and_63_out, a, not_2_out, d, e);
  and and_64 (and_64_out, a, not_2_out, c, not_4_out, not_5_out, not_6_out);
  and and_65 (and_65_out, a, b, not_4_out, e);
  and and_66 (and_66_out, a, b, c, d, f);
  and and_67 (and_67_out, not_1_out, not_4_out, not_5_out, not_6_out);
  and and_68 (and_68_out, not_2_out, not_3_out, not_4_out, not_5_out);
  and and_69 (and_69_out, not_1_out, not_2_out, not_3_out, d);
  and and_70 (and_70_out, not_3_out, d, e, not_6_out);
  and and_71 (and_71_out, not_1_out, not_2_out, c, e, f);
  and and_72 (and_72_out, not_2_out, c, d, f);
  and and_73 (and_73_out, c, d, e, f);
  and and_74 (and_74_out, b, not_3_out, not_4_out, e, f);
  and and_75 (and_75_out, b, c, not_4_out, not_5_out);
  and and_76 (and_76_out, a, not_2_out, not_3_out, e, f);
  and and_77 (and_77_out, a, b, not_4_out, f);
  and and_78 (and_78_out, a, b, not_5_out, f);
  and and_79 (and_79_out, a, b, not_3_out, d, not_5_out);
  or or_1 (u, and_1_out, and_2_out, and_3_out, and_4_out, and_5_out, and_6_out, and_7_out, and_8_out, and_9_out, and_10_out, and_11_out, and_12_out, and_13_out);
  or or_2 (v, and_14_out, and_15_out, and_16_out, and_17_out, and_18_out, and_19_out, and_20_out, and_21_out, and_22_out, and_23_out, and_24_out);
  or or_3 (w, and_25_out, and_26_out, and_27_out, and_28_out, and_29_out, and_30_out, and_31_out, and_32_out, and_33_out, and_34_out, and_35_out, and_36_out, and_37_out);
  or or_4 (x, and_38_out, and_39_out, and_40_out, and_41_out, and_42_out, and_43_out, and_44_out, and_45_out, and_46_out, and_47_out, and_48_out, and_49_out, and_50_out, and_51_out, and_52_out);
  or or_5 (y, and_53_out, and_54_out, and_55_out, and_56_out, and_57_out, and_58_out, and_59_out, and_60_out, and_61_out, and_62_out, and_63_out, and_64_out, and_65_out, and_66_out);
  or or_6 (z, and_67_out, and_68_out, and_69_out, and_70_out, and_71_out, and_72_out, and_73_out, and_74_out, and_75_out, and_76_out, and_77_out, and_78_out, and_79_out);
endmodule

module Circuit_Action (
  input  a,
  input  b,
  input  c,
  input  d,
  input  e,
  input  f,
  output x,
  output y
);

  wire and_1_out, and_2_out, and_3_out, and_4_out, and_5_out, and_6_out, and_7_out, and_8_out, and_9_out,
       and_10_out, and_11_out, and_12_out, and_13_out, and_14_out, not_1_out, not_2_out, not_3_out,
       not_4_out, not_5_out, not_6_out;

  not not_1 (not_1_out, a);
  not not_2 (not_2_out, b);
  not not_3 (not_3_out, c);
  not not_4 (not_4_out, d);
  not not_5 (not_5_out, e);
  not not_6 (not_6_out, f);
  and and_1 (and_1_out, not_1_out, not_2_out, not_5_out, f);
  and and_2 (and_2_out, not_1_out, not_2_out, d, e);
  and and_3 (and_3_out, not_1_out, not_2_out, c, not_4_out);
  and and_4 (and_4_out, not_1_out, c, not_4_out, f);
  and and_5 (and_5_out, not_1_out, c, e);
  and and_6 (and_6_out, b, not_3_out, not_4_out, not_5_out, not_6_out);
  and and_7 (and_7_out, b, c, d, not_6_out);
  and and_8 (and_8_out, not_2_out, not_3_out, not_5_out);
  and and_9 (and_9_out, not_1_out, not_2_out, c, e);
  and and_10 (and_10_out, b, e, not_6_out);
  and and_11 (and_11_out, b, d, not_5_out, f);
  and and_12 (and_12_out, not_1_out, b, not_3_out, d, e);
  and and_13 (and_13_out, a, not_3_out, not_4_out);
  and and_14 (and_14_out, a, not_3_out, not_5_out);
  or or_1 (x, and_1_out, and_2_out, and_3_out, and_4_out, and_5_out, and_6_out, and_7_out);
  or or_2 (y, and_8_out, and_9_out, and_10_out, and_11_out, and_12_out, and_13_out, and_14_out);
endmodule

module Circuit_two_7_Segment (
  input  [5:0] Entrance,
  output da,
  output db,
  output dc,
  output dd,
  output de,
  output df,
  output dg,
  output ua,
  output ub,
  output uc,
  output ud,
  output ue,
  output uf,
  output ug
);

  wire and_1_out, and_2_out, and_3_out, and_4_out, and_5_out, and_6_out, and_7_out, and_8_out, and_9_out,
       and_10_out, and_11_out, and_12_out, and_13_out, and_14_out, and_15_out, and_16_out, and_17_out,
       and_18_out, and_19_out, and_20_out, and_21_out, and_22_out, and_23_out, and_24_out, and_25_out,
       and_26_out, and_27_out, and_28_out, and_29_out, and_30_out, and_31_out, and_32_out, and_33_out,
       and_34_out, and_35_out, and_36_out, and_37_out, and_38_out, and_39_out, and_40_out, and_41_out,
       and_42_out, and_43_out, and_44_out, and_45_out, and_46_out, and_47_out, and_48_out, and_49_out,
       and_50_out, and_51_out, and_52_out, and_53_out, and_54_out, and_55_out, and_56_out, and_57_out,
       and_58_out, and_59_out, and_60_out, and_61_out, and_62_out, and_63_out, and_64_out, and_65_out,
       and_66_out, and_67_out, and_68_out, and_69_out, and_70_out, and_71_out, and_72_out, and_73_out,
       and_74_out, and_75_out, and_76_out, and_77_out, and_78_out, and_79_out, and_80_out, and_81_out,
       and_82_out, and_83_out, and_84_out, and_85_out, and_86_out, and_87_out, and_88_out, and_89_out,
       and_90_out, and_91_out, and_92_out, and_93_out, and_94_out, and_95_out, and_96_out, and_97_out,
       and_98_out, and_99_out, and_100_out, and_101_out, and_102_out, and_103_out, and_104_out, and_105_out,
       and_106_out, and_107_out, and_108_out, and_109_out, and_110_out, and_111_out, and_112_out,
       and_113_out, and_114_out, and_115_out, and_116_out, and_117_out, and_118_out, and_119_out,
       and_120_out, and_121_out, and_122_out, and_123_out, and_124_out, and_125_out, and_126_out,
       and_127_out, and_128_out, and_129_out, and_130_out, not_1_out, not_2_out, not_3_out, not_4_out,
       not_5_out, not_6_out;

  not not_1 (not_1_out, Entrance[5]);
  not not_2 (not_2_out, Entrance[4]);
  not not_3 (not_3_out, Entrance[3]);
  not not_4 (not_4_out, Entrance[2]);
  not not_5 (not_5_out, Entrance[1]);
  not not_6 (not_6_out, Entrance[0]);
  and and_1 (and_1_out, not_1_out, not_2_out, not_4_out, not_6_out);
  and and_2 (and_2_out, not_1_out, not_3_out, Entrance[1]);
  and and_3 (and_3_out, not_2_out, Entrance[2], Entrance[0]);
  and and_4 (and_4_out, not_1_out, not_2_out, Entrance[3], not_5_out);
  and and_5 (and_5_out, not_1_out, Entrance[3], Entrance[2], not_5_out);
  and and_6 (and_6_out, not_1_out, Entrance[4], not_3_out, not_6_out);
  and and_7 (and_7_out, Entrance[4], not_3_out, not_4_out, not_6_out);
  and and_8 (and_8_out, not_1_out, Entrance[4], not_4_out, Entrance[0]);
  and and_9 (and_9_out, not_1_out, Entrance[4], Entrance[1], not_6_out);
  and and_10 (and_10_out, Entrance[5], not_3_out, not_5_out);
  and and_11 (and_11_out, Entrance[5], not_4_out, not_5_out, not_6_out);
  and and_12 (and_12_out, Entrance[5], not_2_out, not_3_out, Entrance[0]);
  and and_13 (and_13_out, Entrance[5], not_2_out, not_3_out, Entrance[2]);
  and and_14 (and_14_out, Entrance[5], not_3_out, Entrance[2], Entrance[0]);
  and and_15 (and_15_out, Entrance[5], Entrance[3], Entrance[1]);
  and and_16 (and_16_out, Entrance[5], Entrance[4], not_4_out, not_5_out);
  and and_17 (and_17_out, Entrance[5], Entrance[4], not_5_out, not_6_out);
  and and_18 (and_18_out, not_1_out, not_2_out, not_4_out);
  and and_19 (and_19_out, not_1_out, not_2_out, not_5_out, not_6_out);
  and and_20 (and_20_out, not_2_out, not_4_out, not_5_out);
  and and_21 (and_21_out, not_1_out, not_3_out, not_4_out, Entrance[0]);
  and and_22 (and_22_out, not_1_out, not_3_out, not_4_out, Entrance[1]);
  and and_23 (and_23_out, not_1_out, not_3_out, Entrance[1], Entrance[0]);
  and and_24 (and_24_out, not_1_out, not_4_out, Entrance[1], Entrance[0]);
  and and_25 (and_25_out, not_1_out, not_2_out, Entrance[3], not_5_out);
  and and_26 (and_26_out, not_1_out, not_2_out, Entrance[3], not_6_out);
  and and_27 (and_27_out, not_1_out, Entrance[3], not_5_out, not_6_out);
  and and_28 (and_28_out, not_2_out, Entrance[3], not_5_out, not_6_out);
  and and_29 (and_29_out, not_1_out, Entrance[4], Entrance[2]);
  and and_30 (and_30_out, Entrance[4], Entrance[2], not_5_out);
  and and_31 (and_31_out, Entrance[4], Entrance[3], Entrance[2]);
  and and_32 (and_32_out, Entrance[5], not_4_out, not_5_out, Entrance[0]);
  and and_33 (and_33_out, Entrance[5], not_3_out, Entrance[1], not_6_out);
  and and_34 (and_34_out, Entrance[5], not_2_out, not_3_out, Entrance[2], Entrance[0]);
  and and_35 (and_35_out, Entrance[5], Entrance[3], not_4_out, Entrance[1]);
  and and_36 (and_36_out, Entrance[5], Entrance[3], Entrance[1], Entrance[0]);
  and and_37 (and_37_out, Entrance[5], Entrance[4], not_3_out, not_4_out);
  and and_38 (and_38_out, not_1_out, not_3_out, not_5_out);
  and and_39 (and_39_out, not_2_out, not_3_out, Entrance[2]);
  and and_40 (and_40_out, Entrance[3], not_4_out);
  and and_41 (and_41_out, not_2_out, Entrance[3], Entrance[1]);
  and and_42 (and_42_out, Entrance[4], not_4_out);
  and and_43 (and_43_out, not_1_out, Entrance[4], Entrance[3]);
  and and_44 (and_44_out, Entrance[5], not_3_out, Entrance[1]);
  and and_45 (and_45_out, Entrance[5], Entrance[3], not_5_out);
  and and_46 (and_46_out, not_1_out, not_2_out, not_4_out, not_6_out);
  and and_47 (and_47_out, not_2_out, not_4_out, not_5_out, not_6_out);
  and and_48 (and_48_out, not_1_out, not_2_out, not_3_out, not_4_out, Entrance[1]);
  and and_49 (and_49_out, not_1_out, not_2_out, Entrance[2], not_5_out, Entrance[0]);
  and and_50 (and_50_out, not_2_out, not_3_out, Entrance[2], Entrance[1], not_6_out);
  and and_51 (and_51_out, not_1_out, not_2_out, Entrance[3], not_5_out, not_6_out);
  and and_52 (and_52_out, not_1_out, not_2_out, Entrance[3], Entrance[2], Entrance[0]);
  and and_53 (and_53_out, not_2_out, Entrance[3], Entrance[2], not_5_out, Entrance[0]);
  and and_54 (and_54_out, not_1_out, Entrance[4], not_3_out, not_6_out);
  and and_55 (and_55_out, Entrance[4], not_4_out, Entrance[1], not_6_out);
  and and_56 (and_56_out, not_1_out, Entrance[4], Entrance[2], not_6_out);
  and and_57 (and_57_out, not_1_out, Entrance[4], not_3_out, Entrance[2], Entrance[1]);
  and and_58 (and_58_out, not_1_out, Entrance[4], Entrance[3], not_4_out, not_5_out, Entrance[0]);
  and and_59 (and_59_out, Entrance[5], not_2_out, not_3_out, not_4_out, not_5_out);
  and and_60 (and_60_out, Entrance[5], not_3_out, not_5_out, not_6_out);
  and and_61 (and_61_out, Entrance[5], not_2_out, not_4_out, Entrance[1], Entrance[0]);
  and and_62 (and_62_out, Entrance[5], not_2_out, Entrance[2], Entrance[1], not_6_out);
  and and_63 (and_63_out, Entrance[5], Entrance[4], not_3_out, Entrance[2], Entrance[0]);
  and and_64 (and_64_out, Entrance[5], Entrance[4], Entrance[3], not_6_out);
  and and_65 (and_65_out, Entrance[5], Entrance[4], Entrance[3], Entrance[2], Entrance[1]);
  and and_66 (and_66_out, not_1_out, not_2_out, not_4_out, not_6_out);
  and and_67 (and_67_out, not_2_out, not_3_out, Entrance[2], Entrance[1], not_6_out);
  and and_68 (and_68_out, not_1_out, not_2_out, Entrance[3], not_5_out, not_6_out);
  and and_69 (and_69_out, not_1_out, Entrance[4], not_3_out, not_6_out);
  and and_70 (and_70_out, Entrance[4], not_4_out, Entrance[1], not_6_out);
  and and_71 (and_71_out, Entrance[4], Entrance[3], Entrance[2], not_6_out);
  and and_72 (and_72_out, Entrance[5], not_3_out, not_5_out, not_6_out);
  and and_73 (and_73_out, Entrance[5], Entrance[3], not_4_out, not_6_out);
  and and_74 (and_74_out, Entrance[5], Entrance[3], Entrance[1], not_6_out);
  and and_75 (and_75_out, not_1_out, not_3_out, not_5_out, not_6_out);
  and and_76 (and_76_out, not_1_out, not_2_out, not_3_out, Entrance[2], not_5_out);
  and and_77 (and_77_out, not_2_out, not_3_out, Entrance[2], not_6_out);
  and and_78 (and_78_out, not_1_out, Entrance[3], not_4_out, not_5_out);
  and and_79 (and_79_out, Entrance[3], not_4_out, not_6_out);
  and and_80 (and_80_out, not_1_out, not_2_out, Entrance[3], Entrance[2], Entrance[1]);
  and and_81 (and_81_out, Entrance[4], not_4_out, not_6_out);
  and and_82 (and_82_out, not_1_out, Entrance[4], not_3_out, not_4_out, Entrance[1]);
  and and_83 (and_83_out, not_1_out, Entrance[4], Entrance[3], not_5_out);
  and and_84 (and_84_out, not_1_out, Entrance[4], Entrance[3], not_6_out);
  and and_85 (and_85_out, Entrance[5], not_2_out, not_3_out, Entrance[1]);
  and and_86 (and_86_out, Entrance[5], not_3_out, Entrance[2], Entrance[1]);
  and and_87 (and_87_out, Entrance[5], not_2_out, Entrance[3], not_6_out);
  and and_88 (and_88_out, Entrance[5], Entrance[3], not_5_out, not_6_out);
  and and_89 (and_89_out, Entrance[5], not_2_out, Entrance[3], Entrance[2], not_5_out);
  and and_90 (and_90_out, Entrance[5], Entrance[4], not_3_out, not_4_out, not_5_out);
  and and_91 (and_91_out, Entrance[5], Entrance[4], Entrance[3], not_4_out, Entrance[1]);
  and and_92 (and_92_out, not_1_out, not_3_out, not_4_out, Entrance[1]);
  and and_93 (and_93_out, not_1_out, not_2_out, Entrance[2], not_5_out);
  and and_94 (and_94_out, not_2_out, Entrance[2], not_6_out);
  and and_95 (and_95_out, not_1_out, Entrance[3], not_5_out);
  and and_96 (and_96_out, not_1_out, not_2_out, Entrance[3], Entrance[2]);
  and and_97 (and_97_out, not_2_out, Entrance[3], Entrance[2], not_5_out);
  and and_98 (and_98_out, not_1_out, Entrance[4], not_4_out, not_6_out);
  and and_99 (and_99_out, Entrance[4], not_4_out, not_5_out, not_6_out);
  and and_100 (and_100_out, Entrance[4], not_3_out, Entrance[2], Entrance[1]);
  and and_101 (and_101_out, Entrance[5], not_2_out, not_3_out, not_4_out);
  and and_102 (and_102_out, Entrance[5], not_2_out, not_3_out, Entrance[1]);
  and and_103 (and_103_out, Entrance[5], Entrance[3], not_4_out, Entrance[1]);
  and and_104 (and_104_out, Entrance[5], Entrance[4], not_3_out, not_5_out);
  and and_105 (and_105_out, Entrance[5], Entrance[4], Entrance[3], Entrance[1]);
  and and_106 (and_106_out, not_1_out, not_2_out, not_4_out, not_5_out);
  and and_107 (and_107_out, not_2_out, not_3_out);
  and and_108 (and_108_out, not_3_out, Entrance[2]);
  and and_109 (and_109_out, Entrance[4], Entrance[3]);
  and and_110 (and_110_out, Entrance[5], not_3_out, Entrance[1]);
  and and_111 (and_111_out, not_3_out, not_4_out, not_5_out);
  and and_112 (and_112_out, not_3_out, not_4_out);
  and and_113 (and_113_out, Entrance[3], Entrance[2], Entrance[1]);
  and and_114 (and_114_out, not_1_out, not_2_out, not_4_out, not_5_out);
  and and_115 (and_115_out, not_2_out, not_3_out);
  and and_116 (and_116_out, not_3_out, Entrance[2]);
  and and_117 (and_117_out, Entrance[4], Entrance[3]);
  and and_118 (and_118_out, Entrance[5], not_3_out, Entrance[1]);
  and and_119 (and_119_out, not_1_out, not_2_out, not_3_out);
  and and_120 (and_120_out, not_1_out, not_2_out, not_4_out, not_5_out);
  and and_121 (and_121_out, not_1_out, not_3_out, Entrance[2]);
  and and_122 (and_122_out, not_1_out, Entrance[4], Entrance[3], not_4_out);
  and and_123 (and_123_out, not_1_out, Entrance[4], Entrance[3], not_5_out);
  and and_124 (and_124_out, Entrance[5], Entrance[4], Entrance[3], Entrance[2]);
  and and_125 (and_125_out, not_1_out, not_2_out, not_3_out);
  and and_126 (and_126_out, not_1_out, not_2_out, not_4_out, not_5_out);
  and and_127 (and_127_out, Entrance[5], Entrance[3]);
  and and_128 (and_128_out, Entrance[5], Entrance[4]);
  and and_129 (and_129_out, Entrance[4], Entrance[2]);
  and and_130 (and_130_out, Entrance[4], Entrance[3]);
  or or_1 (dc, and_38_out, Entrance[0], and_39_out, and_40_out, and_41_out, and_42_out, and_43_out, and_44_out, and_45_out);
  or or_2 (de, and_66_out, and_67_out, and_68_out, and_69_out, and_70_out, and_71_out, and_72_out, and_73_out, and_74_out);
  or or_3 (ua, and_106_out, and_107_out, and_108_out, and_109_out, and_110_out);
  or or_4 (ub, not_1_out, not_2_out, and_111_out);
  or or_5 (uc, not_2_out, and_112_out, and_113_out, Entrance[5]);
  or or_6 (ud, and_114_out, and_115_out, and_116_out, and_117_out, and_118_out);
  or or_7 (ue, and_119_out, and_120_out, and_121_out, and_122_out, and_123_out, and_124_out);
  or or_8 (uf, and_125_out, and_126_out, and_127_out, and_128_out);
  or or_9 (ug, and_129_out, and_130_out, Entrance[5]);
  or or_10 (da, and_1_out, and_2_out, and_3_out, and_4_out, and_5_out, and_6_out, and_7_out, and_8_out, and_9_out, and_10_out, and_11_out, and_12_out, and_13_out, and_14_out, and_15_out, and_16_out, and_17_out);
  or or_11 (db, and_18_out, and_19_out, and_20_out, and_21_out, and_22_out, and_23_out, and_24_out, and_25_out, and_26_out, and_27_out, and_28_out, and_29_out, and_30_out, and_31_out, and_32_out, and_33_out, and_34_out, and_35_out, and_36_out, and_37_out);
  or or_12 (dd, and_46_out, and_47_out, and_48_out, and_49_out, and_50_out, and_51_out, and_52_out, and_53_out, and_54_out, and_55_out, and_56_out, and_57_out, and_58_out, and_59_out, and_60_out, and_61_out, and_62_out, and_63_out, and_64_out, and_65_out);
  or or_13 (df, and_75_out, and_76_out, and_77_out, and_78_out, and_79_out, and_80_out, and_81_out, and_82_out, and_83_out, and_84_out, and_85_out, and_86_out, and_87_out, and_88_out, and_89_out, and_90_out, and_91_out);
  or or_14 (dg, and_92_out, and_93_out, and_94_out, and_95_out, and_96_out, and_97_out, and_98_out, and_99_out, and_100_out, and_101_out, and_102_out, and_103_out, and_104_out, and_105_out);
endmodule

module Display_Decoder (
  input  [6:0] in_1
);

  _7_Segment_Display u_7_segment_display_1 (
    .g(in_1[6]), .f(in_1[5]), .a(in_1[0]), .b(in_1[1]), .e(in_1[4]), .d(in_1[3]), .c(in_1[2]));  // open: dp
endmodule

module Binary_to_Two_7_Segment_Decoder (
  input  [5:0] Entrance,
  output [6:0] Display_2,
  output [6:0] Display_1
);

  Circuit_two_7_Segment circuit_two_7_segment_1 (
    .db(Display_2[1]), .dc(Display_2[2]), .dd(Display_2[3]), .de(Display_2[4]), .df(Display_2[5]),
    .dg(Display_2[6]), .ua(Display_1[0]), .ub(Display_1[1]), .uc(Display_1[2]), .ud(Display_1[3]),
    .ue(Display_1[4]), .uf(Display_1[5]), .ug(Display_1[6]), .da(Display_2[0]), .Entrance(Entrance));
endmodule

module Movement_Control_Decoder (
  input  [5:0] Entrance,
  output [5:0] Next_Position,
  output [1:0] Action
);

  Circuit_Movement circuit_movement_1 (
    .w(Next_Position[3]), .x(Next_Position[2]), .y(Next_Position[1]), .z(Next_Position[0]),
    .u(Next_Position[5]), .v(Next_Position[4]), .c(Entrance[3]), .d(Entrance[2]), .e(Entrance[1]),
    .f(Entrance[0]), .a(Entrance[5]), .b(Entrance[4]));
  Circuit_Action circuit_action_1 (
    .x(Action[1]), .y(Action[0]), .c(Entrance[3]), .d(Entrance[2]), .e(Entrance[1]), .f(Entrance[0]),
    .a(Entrance[5]), .b(Entrance[4]));
endmodule

module Action_Decoder (
  input  [1:0] Entrance,
  output Right_Go,
  output Left_Go,
  output Go,
  output Stop
);

  wire not_1_out, not_2_out;

  not not_1 (not_1_out, Entrance[1]);
  not not_2 (not_2_out, Entrance[0]);
  and and_1 (Right_Go, not_1_out, not_2_out);
  and and_2 (Left_Go, Entrance[1], not_2_out);
  and and_3 (Go, not_1_out, Entrance[0]);
  and and_4 (Stop, Entrance[1], Entrance[0]);
endmodule
