// Logisim project Juego.circ as structural Verilog: 7 circuits, main circuit main
module main (
);

  wire button_1_out, clock_1_out, clock_2_out, start_counter_1_catch, start_counter_1_not_cath,
       start_counter_1_reset_out;
  wire [1:0] joystick_1_x;
  wire [15:0] control_decoder_1_control_out, screen_decoder_1_row1, screen_decoder_1_row2,
       screen_decoder_1_row3, screen_decoder_1_row4, screen_decoder_1_row5, screen_decoder_1_row6,
       screen_decoder_1_row7, screen_decoder_1_row8, screen_decoder_1_row9, screen_decoder_1_row10,
       screen_decoder_1_row11, screen_decoder_1_row12, screen_decoder_1_row13, screen_decoder_1_row14,
       screen_decoder_1_row15, screen_decoder_1_row16;

  Clock clock_1 (.out(clock_1_out));
  DotMatrix #(.dotshape("circle"), .inputtype("row"), .matrixcols(16), .matrixrows(16)) dotmatrix_1 (
    .row0(screen_decoder_1_row1), .row1(screen_decoder_1_row2), .row2(screen_decoder_1_row3),
    .row3(screen_decoder_1_row4), .row4(screen_decoder_1_row5), .row5(screen_decoder_1_row6),
    .row6(screen_decoder_1_row7), .row7(screen_decoder_1_row8), .row8(screen_decoder_1_row9),
    .row9(screen_decoder_1_row10), .row10(screen_decoder_1_row11), .row11(screen_decoder_1_row12),
    .row12(screen_decoder_1_row13), .row13(screen_decoder_1_row14), .row14(screen_decoder_1_row15),
    .row15(screen_decoder_1_row16));
  screen_decoder screen_decoder_1 (
    .row1(screen_decoder_1_row1), .row2(screen_decoder_1_row2), .row3(screen_decoder_1_row3),
    .row4(screen_decoder_1_row4), .row5(screen_decoder_1_row5), .row6(screen_decoder_1_row6),
    .row7(screen_decoder_1_row7), .row8(screen_decoder_1_row8), .row9(screen_decoder_1_row9),
    .row10(screen_decoder_1_row10), .row11(screen_decoder_1_row11), .row12(screen_decoder_1_row12),
    .row13(screen_decoder_1_row13), .row14(screen_decoder_1_row14), .row15(screen_decoder_1_row15),
    .row16(screen_decoder_1_row16), .Reset(button_1_out), .Clock(clock_2_out));
  DotMatrix #(.dotshape("circle"), .inputtype("row"), .matrixcols(16), .matrixrows(1)) dotmatrix_2 (.row0(control_decoder_1_control_out));
  control_decoder control_decoder_1 (
    .control_out(control_decoder_1_control_out), .Reset(button_1_out), .Clock(clock_1_out),
    .joystick_in(joystick_1_x));
  Button button_1 (.out(button_1_out));
  Joystick #(.bits(2)) joystick_1 (.x(joystick_1_x));  // open: y
  counter_flip_flop counter_flip_flop_1 (.reset(start_counter_1_reset_out), .a(start_counter_1_catch));
  counter_flip_flop counter_flip_flop_2 (.reset(start_counter_1_reset_out), .a(start_counter_1_not_cath));
  start_counter start_counter_1 (
    .not_cath(start_counter_1_not_cath), .reset_out(start_counter_1_reset_out),
    .catch(start_counter_1_catch), .reset_in(button_1_out), .Clock_in(clock_2_out),
    .last_row_screen(screen_decoder_1_row16), .joystick_out(control_decoder_1_control_out));
  Clock #(.highDuration(8), .lowDuration(8)) clock_2 (.out(clock_2_out));

  // Notes on the sheet:
  //   Catch
  //   Not Catch
endmodule

module start_counter (
  input  [15:0] last_row_screen,
  input  [15:0] joystick_out,
  input  reset_in,
  input  Clock_in,
  output catch,
  output not_cath,
  output reset_out
);

  wire comparator_1_eq, comparator_1_gt, comparator_1_lt, comparator_2_gt, comparator_2_lt, d_ff_1_qn,
       or_1_out, or_2_out;

  Comparator #(.width(16)) comparator_1 (
    .a(last_row_screen), .b(joystick_out), .gt(comparator_1_gt), .eq(comparator_1_eq), .lt(comparator_1_lt));
  Comparator #(.width(16)) comparator_2 (
    .a(last_row_screen), .b({16{1'b0}}), .gt(comparator_2_gt), .lt(comparator_2_lt));  // open: eq
  or or_1 (or_1_out, comparator_1_gt, comparator_1_lt);
  or or_2 (or_2_out, comparator_2_gt, comparator_2_lt);
  D_Flip_Flop d_ff_1 (.D(comparator_1_eq), .clk(Clock_in), .Q(catch), .Qn(d_ff_1_qn));  // open: preset, reset
  and and_1 (not_cath, d_ff_1_qn, or_1_out, Clock_in, or_2_out);

  assign reset_out = reset_in;

  // Notes on the sheet:
  //   estrella atrapada
  //   estrella no atrapada
endmodule

module counter_flip_flop (
  input  a,
  input  reset
);

  wire j_k_ff_1_q, j_k_ff_1_qn, j_k_ff_2_q, j_k_ff_2_qn, j_k_ff_3_q, j_k_ff_3_qn, j_k_ff_4_q,
       sevent_segment_1_a, sevent_segment_1_b, sevent_segment_1_c, sevent_segment_1_d, sevent_segment_1_e,
       sevent_segment_1_f, sevent_segment_1_g;

  J_K_Flip_Flop j_k_ff_1 (
    .J(1'b1), .K(1'b1), .clk(a), .Q(j_k_ff_1_q), .Qn(j_k_ff_1_qn), .reset(reset));  // open: preset
  J_K_Flip_Flop j_k_ff_2 (
    .J(1'b1), .K(1'b1), .clk(j_k_ff_1_qn), .Q(j_k_ff_2_q), .Qn(j_k_ff_2_qn), .reset(reset));  // open: preset
  J_K_Flip_Flop j_k_ff_3 (
    .J(1'b1), .K(1'b1), .clk(j_k_ff_2_qn), .Q(j_k_ff_3_q), .Qn(j_k_ff_3_qn), .reset(reset));  // open: preset
  J_K_Flip_Flop j_k_ff_4 (.J(1'b1), .K(1'b1), .clk(j_k_ff_3_qn), .Q(j_k_ff_4_q), .reset(reset));  // open: Qn, preset
  sevent_segment sevent_segment_1 (
    .c(sevent_segment_1_c), .d(sevent_segment_1_d), .e(sevent_segment_1_e), .f(sevent_segment_1_f),
    .g(sevent_segment_1_g), .a(sevent_segment_1_a), .b(sevent_segment_1_b), .Y(j_k_ff_2_q), .Z(j_k_ff_1_q),
    .W(j_k_ff_4_q), .X(j_k_ff_3_q));
  _7_Segment_Display u_7_segment_display_1 (
    .g(sevent_segment_1_g), .f(sevent_segment_1_f), .a(sevent_segment_1_a), .b(sevent_segment_1_b),
    .e(sevent_segment_1_e), .d(sevent_segment_1_d), .c(sevent_segment_1_c));  // open: dp
endmodule

module sevent_segment (
  input  W,
  input  X,
  input  Y,
  input  Z,
  output a,
  output b,
  output c,
  output d,
  output e,
  output f,
  output g
);

  wire and_1_out, and_2_out, and_3_out, and_4_out, and_5_out, and_6_out, and_7_out, and_8_out, and_9_out,
       and_10_out, and_11_out, and_12_out, and_13_out, and_14_out, and_15_out, and_16_out, and_17_out,
       and_18_out, and_19_out, and_20_out, and_21_out, and_22_out, and_23_out, and_24_out, and_25_out,
       and_26_out, and_27_out, and_28_out, and_29_out, and_30_out, and_31_out, and_32_out, and_33_out,
       and_34_out, and_35_out, and_36_out, and_37_out, and_38_out, and_39_out, and_40_out, and_41_out,
       and_42_out, and_43_out, and_44_out, and_45_out, and_46_out, and_47_out, not_1_out, not_2_out,
       not_3_out, not_4_out, or_1_out, or_2_out, or_3_out, or_4_out, or_5_out, or_6_out, or_7_out, or_8_out,
       or_9_out, or_10_out, or_11_out, or_12_out, or_14_out, or_15_out, or_16_out, or_17_out, or_19_out,
       or_20_out, or_21_out, or_22_out, or_24_out;

  not not_1 (not_1_out, W);
  not not_2 (not_2_out, X);
  not not_3 (not_3_out, Y);
  not not_4 (not_4_out, Z);
  and and_1 (and_1_out, W, not_2_out);
  and and_2 (and_2_out, not_1_out, not_3_out);
  and and_3 (and_3_out, not_1_out, not_3_out);
  and and_4 (and_4_out, not_1_out, Z);
  and and_5 (and_5_out, not_1_out, not_2_out);
  and and_6 (and_6_out, not_2_out, Y);
  and and_7 (and_7_out, not_2_out, not_4_out);
  and and_8 (and_8_out, Y, not_4_out);
  and and_9 (and_9_out, W, Y);
  and and_10 (and_10_out, W, X);
  and and_11 (and_11_out, not_1_out, X);
  and and_12 (and_12_out, not_2_out, Y);
  and and_13 (and_13_out, Y, not_4_out);
  and and_14 (and_14_out, not_1_out, X);
  and and_15 (and_15_out, not_2_out, not_4_out);
  and and_16 (and_16_out, not_1_out, Y);
  and and_17 (and_17_out, not_1_out, X);
  and and_18 (and_18_out, X, Y);
  and and_19 (and_19_out, and_1_out, not_3_out);
  and and_20 (and_20_out, not_1_out, not_2_out);
  and and_21 (and_21_out, and_2_out, not_4_out);
  and and_22 (and_22_out, not_1_out, Y);
  and and_23 (and_23_out, W, not_3_out);
  or or_1 (or_1_out, and_3_out, and_4_out);
  and and_24 (and_24_out, not_3_out, Z);
  and and_25 (and_25_out, not_1_out, X);
  and and_26 (and_26_out, W, not_2_out);
  and and_27 (and_27_out, and_5_out, not_4_out);
  and and_28 (and_28_out, and_6_out, Z);
  and and_29 (and_29_out, X, not_3_out);
  and and_30 (and_30_out, X, Y);
  and and_31 (and_31_out, W, not_3_out);
  or or_2 (or_2_out, and_7_out, and_8_out);
  or or_3 (or_3_out, and_9_out, and_10_out);
  and and_32 (and_32_out, not_3_out, not_4_out);
  and and_33 (and_33_out, and_11_out, not_3_out);
  or or_4 (or_4_out, and_12_out, and_13_out);
  and and_34 (and_34_out, and_14_out, not_3_out);
  and and_35 (and_35_out, W, not_2_out);
  and and_36 (and_36_out, W, Z);
  or or_5 (or_5_out, and_15_out, and_16_out);
  or or_6 (or_6_out, or_5_out, and_37_out);
  and and_37 (and_37_out, and_17_out, Z);
  or or_7 (or_7_out, and_18_out, and_19_out);
  or or_8 (or_8_out, or_7_out, and_38_out);
  and and_38 (and_38_out, W, not_4_out);
  or or_9 (or_9_out, and_20_out, and_21_out);
  or or_10 (or_10_out, or_9_out, and_39_out);
  and and_39 (and_39_out, not_2_out, not_4_out);
  and and_40 (and_40_out, and_22_out, Z);
  or or_11 (or_11_out, and_40_out, and_41_out);
  and and_41 (and_41_out, and_23_out, Z);
  or or_12 (or_12_out, or_1_out, and_24_out);
  or or_13 (c, or_12_out, or_14_out);
  or or_14 (or_14_out, and_25_out, and_26_out);
  or or_15 (or_15_out, and_27_out, and_28_out);
  or or_16 (or_16_out, or_15_out, and_42_out);
  and and_42 (and_42_out, and_29_out, Z);
  and and_43 (and_43_out, and_30_out, not_4_out);
  or or_17 (or_17_out, and_43_out, and_44_out);
  and and_44 (and_44_out, and_31_out, not_4_out);
  or or_18 (e, or_2_out, or_3_out);
  or or_19 (or_19_out, and_32_out, and_33_out);
  or or_20 (or_20_out, or_19_out, and_45_out);
  and and_45 (and_45_out, X, not_4_out);
  and and_46 (and_46_out, W, not_2_out);
  or or_21 (or_21_out, and_46_out, and_47_out);
  and and_47 (and_47_out, W, Y);
  or or_22 (or_22_out, or_4_out, and_34_out);
  or or_23 (g, or_22_out, or_24_out);
  or or_24 (or_24_out, and_35_out, and_36_out);
  or or_25 (a, or_6_out, or_8_out);
  or or_26 (b, or_10_out, or_11_out);
  or or_27 (d, or_16_out, or_17_out);
  or or_28 (f, or_20_out, or_21_out);
endmodule

module control_decoder (
  input  Reset,
  input  [1:0] joystick_in,
  input  Clock,
  output [15:0] control_out
);

  wire [3:0] counter_1_q;

  Counter #(.max('hf), .width(4)) counter_1 (
    .clr(Reset), .up(joystick_in[1]), .count(joystick_in[0]), .clk(Clock), .Q(counter_1_q));  // open: load, D, carry
  Decoder #(.select(4)) decoder_1 (
    .out0(control_out[0]), .out1(control_out[1]), .out2(control_out[2]), .out3(control_out[3]),
    .out4(control_out[4]), .out5(control_out[5]), .out6(control_out[6]), .out7(control_out[7]),
    .out8(control_out[8]), .out9(control_out[9]), .out10(control_out[10]), .out11(control_out[11]),
    .out12(control_out[12]), .out13(control_out[13]), .out14(control_out[14]), .out15(control_out[15]),
    .sel(counter_1_q));  // open: en
endmodule

module screen_decoder (
  input  Reset,
  input  Clock,
  output [15:0] row1,
  output [15:0] row2,
  output [15:0] row3,
  output [15:0] row4,
  output [15:0] row5,
  output [15:0] row6,
  output [15:0] row7,
  output [15:0] row8,
  output [15:0] row9,
  output [15:0] row10,
  output [15:0] row11,
  output [15:0] row12,
  output [15:0] row13,
  output [15:0] row14,
  output [15:0] row15,
  output [15:0] row16
);

  wire [3:0] random_1_out;
  wire [15:0] decoder_1_out0;

  Random #(.width(4)) random_1 (.clr(Reset), .clk(Clock), .out(random_1_out));  // open: next
  Decoder #(.select(4)) decoder_1 (
    .out0(decoder_1_out0[0]), .out1(decoder_1_out0[1]), .out2(decoder_1_out0[2]), .out3(decoder_1_out0[3]),
    .out4(decoder_1_out0[4]), .out5(decoder_1_out0[5]), .out6(decoder_1_out0[6]), .out7(decoder_1_out0[7]),
    .out8(decoder_1_out0[8]), .out9(decoder_1_out0[9]), .out10(decoder_1_out0[10]),
    .out11(decoder_1_out0[11]), .out12(decoder_1_out0[12]), .out13(decoder_1_out0[13]),
    .out14(decoder_1_out0[14]), .out15(decoder_1_out0[15]), .sel(random_1_out));  // open: en
  // Shift_Register #(.length(16), .width(16)) shift_register_1: pin names not known; wires that end beside it: Reset, Clock, decoder_1_out0, row1, row2, row3, row4, row5, row6, row7, row8, row9, row10, row11, row12
endmodule

module test (
  output reset_out
);

  wire and_1_out, clock_1_out, clock_2_out, comparator_1_eq, comparator_1_gt, comparator_1_lt,
       comparator_2_gt, comparator_2_lt, d_ff_1_q, d_ff_1_qn, or_1_out, or_2_out;
  wire [1:0] joystick_1_x;
  wire [15:0] control_decoder_1_control_out, screen_decoder_1_row1, screen_decoder_1_row2,
       screen_decoder_1_row3, screen_decoder_1_row4, screen_decoder_1_row5, screen_decoder_1_row6,
       screen_decoder_1_row7, screen_decoder_1_row8, screen_decoder_1_row9, screen_decoder_1_row10,
       screen_decoder_1_row11, screen_decoder_1_row12, screen_decoder_1_row13, screen_decoder_1_row14,
       screen_decoder_1_row15, screen_decoder_1_row16;

  Clock clock_1 (.out(clock_1_out));
  DotMatrix #(.dotshape("circle"), .inputtype("row"), .matrixcols(16), .matrixrows(16)) dotmatrix_1 (
    .row0(screen_decoder_1_row1), .row1(screen_decoder_1_row2), .row2(screen_decoder_1_row3),
    .row3(screen_decoder_1_row4), .row4(screen_decoder_1_row5), .row5(screen_decoder_1_row6),
    .row6(screen_decoder_1_row7), .row7(screen_decoder_1_row8), .row8(screen_decoder_1_row9),
    .row9(screen_decoder_1_row10), .row10(screen_decoder_1_row11), .row11(screen_decoder_1_row12),
    .row12(screen_decoder_1_row13), .row13(screen_decoder_1_row14), .row14(screen_decoder_1_row15),
    .row15(screen_decoder_1_row16));
  screen_decoder screen_decoder_1 (
    .row1(screen_decoder_1_row1), .row2(screen_decoder_1_row2), .row3(screen_decoder_1_row3),
    .row4(screen_decoder_1_row4), .row5(screen_decoder_1_row5), .row6(screen_decoder_1_row6),
    .row7(screen_decoder_1_row7), .row8(screen_decoder_1_row8), .row9(screen_decoder_1_row9),
    .row10(screen_decoder_1_row10), .row11(screen_decoder_1_row11), .row12(screen_decoder_1_row12),
    .row13(screen_decoder_1_row13), .row14(screen_decoder_1_row14), .row15(screen_decoder_1_row15),
    .row16(screen_decoder_1_row16), .Reset(reset_out), .Clock(clock_2_out));
  DotMatrix #(.dotshape("circle"), .inputtype("row"), .matrixcols(16), .matrixrows(1)) dotmatrix_2 (.row0(control_decoder_1_control_out));
  control_decoder control_decoder_1 (
    .control_out(control_decoder_1_control_out), .Reset(reset_out), .Clock(clock_1_out),
    .joystick_in(joystick_1_x));
  Button button_1 (.out(reset_out));
  Joystick #(.bits(2)) joystick_1 (.x(joystick_1_x));  // open: y
  counter_flip_flop counter_flip_flop_1 (.reset(reset_out), .a(d_ff_1_q));
  counter_flip_flop counter_flip_flop_2 (.reset(reset_out), .a(and_1_out));
  Comparator #(.width(16)) comparator_1 (
    .a(screen_decoder_1_row16), .b(control_decoder_1_control_out), .gt(comparator_1_gt),
    .eq(comparator_1_eq), .lt(comparator_1_lt));
  Comparator #(.width(16)) comparator_2 (
    .a(screen_decoder_1_row16), .b({16{1'b0}}), .gt(comparator_2_gt), .lt(comparator_2_lt));  // open: eq
  Clock #(.highDuration(8), .lowDuration(8)) clock_2 (.out(clock_2_out));
  or or_1 (or_1_out, comparator_1_gt, comparator_1_lt);
  or or_2 (or_2_out, comparator_2_gt, comparator_2_lt);
  D_Flip_Flop d_ff_1 (.D(comparator_1_eq), .clk(clock_2_out), .Q(d_ff_1_q), .Qn(d_ff_1_qn));  // open: preset, reset
  and and_1 (and_1_out, d_ff_1_qn, or_1_out, or_2_out, clock_2_out);

  // Notes on the sheet:
  //   Catch
  //   Not Catch
  //   estrella atrapada
  //   estrella no atrapada
endmodule
